// Logisim project crc.circ as structural Verilog: 2 circuits, main circuit SRlatch
module main (
);

  wire clock_1_out, \entrée_out , R0_q, R1_q, R2_q, R3_q, Reset_bascules_out, Reset_registre_out, xor_1_out,
       xor_2_out;

  Clock clock_1 (.out(clock_1_out));
  Shift_Register #(.length(14)) \entrée  (
    .clk(clock_1_out), .out(\entrée_out ), .clr(Reset_registre_out));  // open: shift, in, load, d0, q0, d1, q1, d2, q2, d3, q3, d4, q4, d5, q5, d6, q6, d7, q7, d8, q8, d9, q9, d10, q10, d11, q11, d12, q12, d13, q13
  Button Reset_registre (.out(Reset_registre_out));
  Button Reset_bascules (.out(Reset_bascules_out));
  xor xor_1 (xor_1_out, \entrée_out , R3_q);
  D_Flip_Flop R0 (.clk(clock_1_out), .D(xor_1_out), .Q(R0_q), .reset(Reset_bascules_out));  // open: Qn, preset, en
  xor xor_2 (xor_2_out, R0_q, R3_q);
  D_Flip_Flop R1 (.clk(clock_1_out), .D(xor_2_out), .Q(R1_q), .reset(Reset_bascules_out));  // open: Qn, preset, en
  D_Flip_Flop R2 (.clk(clock_1_out), .D(R1_q), .Q(R2_q), .reset(Reset_bascules_out));  // open: Qn, preset, en
  D_Flip_Flop R3 (.clk(clock_1_out), .D(R2_q), .Q(R3_q), .reset(Reset_bascules_out));  // open: Qn, preset, en
  Shift_Register #(.length(14)) sortie (
    .in(R3_q), .clk(clock_1_out));  // open: shift, out, load, clr, d0, q0, d1, q1, d2, q2, d3, q3, d4, q4, d5, q5, d6, q6, d7, q7, d8, q8, d9, q9, d10, q10, d11, q11, d12, q12, d13, q13
endmodule

module SRlatch (
  input  in_1,
  input  in_2,
  output out_3,
  output out_4
);

  nor nor_1 (out_3, in_1, out_4);
  nor nor_2 (out_4, out_3, in_2);
endmodule
